# Fritzing sketch Prototype5 (2) (saved by Fritzing 0.9.8b)
circuit board: 10cm x 10cm

parts:
  BMP388 = Adafruit BMP388 - Barometric Pressure and Altimeter [part_number="Adafruit #3966"]
  GPS_LED = LED - 5mm [color="Green (565nm)" current=0.030 package="5 mm [THT]"]
  IMU1 = 9-DOF Absolute Orientation IMU Fusion Breakout - BNO055
  GPS_module1 = Adafruit Ultimate GPS v3 [part_number="Adafruit #746"]
  SD_card_writer1 = Adafruit MicroSD card breakout board [part_number="Adafruit #254"]
  Status_LED = LED - 5mm [color="Green (565nm)" current=0.030 package="5 mm [THT]"]
  R4 = Resistor [tolerance=±5% resistance=220 power=0.25 package=THT]
  SD_LED = LED - 5mm [color="Green (565nm)" current=0.030 package="5 mm [THT]"]
  R5 = Resistor [tolerance=±5% resistance=220 power=0.25 package=THT]
  5V_LED = LED - 5mm [color="Green (565nm)" current=0.030 package="5 mm [THT]"]
  R6 = Resistor [tolerance=±5% resistance=220 power=0.25 package=THT]
  R7 = Resistor [tolerance=±5% resistance=220 power=0.25 package=THT]
  In+1 = Pad [width=3.5 height=6 connect=center]
  In-1 = Pad [width=3.5 height=6 connect=center]
  Out+1 = Pad [width=3.5 height=6 connect=center]
  Out-1 = Pad [width=3.5 height=6 connect=center]
  Vin = female pin header, 1 pin [form="♀ (female)"]
  GND = female pin header, 1 pin [form="♀ (female)"]
  D2 = Zener Diode [part_number=1N4732A breakdown_voltage=3.6V package="300 mil [THT]"]
  Teensy_3_2 = Teensy 3.1

nets:
  VIN: BMP388.VIN, IMU1.5.0V, GPS_module1.VIN, SD_card_writer1.VCC, R6.Pin_0, In+1.pad, Vin.pin1, Teensy_3_2.Vin
  GND: BMP388.GND, GPS_LED.anode, IMU1.GND, GPS_module1.GND, SD_card_writer1.GND, Status_LED.anode, SD_LED.anode, 5V_LED.anode, In-1.pad, Out-1.pad, GND.pin1, D2.anode, Teensy_3_2.GND, Teensy_3_2.AGND
  N1: BMP388.SCK/SCL, IMU1.SCL_5V, Teensy_3_2.A5/D19
  N2: BMP388.SDI/SDA, IMU1.SDA_5V, Teensy_3_2.A4/D18
  N3: GPS_LED.cathode, R7.Pin_1
  N4: GPS_module1.RX, Teensy_3_2.D1
  N5: GPS_module1.TX, Teensy_3_2.D0
  N6: GPS_module1.FIX, R7.Pin_0
  N7: SD_card_writer1.CLK, Teensy_3_2.D13
  N8: SD_card_writer1.DO, Teensy_3_2.D9
  N9: SD_card_writer1.DI, Teensy_3_2.D10
  N10: SD_card_writer1.CS, Teensy_3_2.A1/D15
  N11: Status_LED.cathode, R4.Pin_1
  N12: R4.Pin_0, Teensy_3_2.D5
  N13: SD_LED.cathode, R5.Pin_1
  N14: R5.Pin_0, Teensy_3_2.D6
  N15: 5V_LED.cathode, R6.Pin_1
  N16: Out+1.pad, D2.cathode

notes:
  Cables
  red - positive
  Black - negative
  pink - I2C
  white - gps pins UART
  Blue - micro SD card reader SPI
  pink - leds
  Crash Sat PCB V5
  By Tejas Vidwans

custom parts:
  9-DOF Absolute Orientation IMU Fusion Breakout - BNO055: A MEMS accelerometer, magnetometer and gyroscope on a single die with a high speed ARM Cortex-M0 based processor to digest all the sensor data, abstract the sensor fusion and real time requirements away, and spit out data you can use in quaternions, Euler angles or vectors.
  Adafruit Ultimate GPS v3: We carry a few different GPS modules here in the Adafruit shop, but none that satisfied our every desire - that's why we designed this little GPS breakout board. We believe this is the Ultimate GPS module, so we named it that. It's got everything you want and more: -165 dBm sensitivity, 10 Hz updates, 66 channels 5V friendly design and only 20mA current draw Breadboard friendly + two mounting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
  Adafruit MicroSD card breakout board: Not just a simple breakout board, this microSD adapter goes the extra mile - designed for ease of use. Onboard 5v->3v regulator provides 150mA for power-hungry cards 3v level shifting means you can use this with ease on either 3v or 5v systems Uses a proper level shifting chip, not resistors: less problems, and faster read/write access Use 3 or 4 digital pins to read and write 2Gb+ of storage!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
